// Logisim project Basic Computer.circ as structural Verilog: 8 circuits, main circuit ALU
module ALU (
  input  [15:0] DR,
  input  [15:0] AC,
  input  [2:0] selection_lines,
  output [15:0] \output ,
  output to_E
);

  wire [15:0] adder_1_out, and_1_out, not_1_out, shifter_1_out, shifter_2_out;

  assign and_1_out = DR & AC;  // AND_Gate and_1, 16 bits wide
  Adder #(.width(16)) adder_1 (.a(DR), .b(AC), .out(adder_1_out), .cin(1'b0), .cout(to_E));
  assign not_1_out = ~AC;  // NOT_Gate not_1, 16 bits wide
  Shifter #(.width(16), .shift("lr")) shifter_1 (.in(AC), .\dist (4'b0001), .out(shifter_1_out));
  Shifter #(.width(16)) shifter_2 (.in(AC), .\dist (4'b0001), .out(shifter_2_out));
  Multiplexer #(.select(3), .width(16)) multiplexer_1 (
    .in0(and_1_out), .in1(adder_1_out), .in2(DR), .in3(not_1_out), .in4(shifter_1_out), .in5(shifter_2_out),
    .out(\output ), .sel(selection_lines), .en(1'b1));  // open: in6, in7
endmodule

module Computer (
  input  Write,
  input  Read,
  input  load,
  input  [2:0] BUS_Sel,
  input  INR,
  input  CLR,
  input  load_2,
  input  INR_2,
  input  CLR_2,
  input  load_3,
  input  INR_3,
  input  CLR_3,
  input  load_4,
  input  INR_4,
  input  [2:0] ALU_selection_lines,
  input  CLR_4,
  input  load_5,
  input  CLR_SC,
  input  load_6,
  input  INR_5,
  input  CLR_5,
  input  D0,
  input  D1,
  input  D2,
  input  D4,
  input  T5,
  input  D3,
  input  in_28,
  input  T4,
  input  D6,
  input  in_31,
  input  in_32,
  input  T6,
  output E
);

  wire AC_cla, AC_inc, AC_lda, ALU_to_e, and_1_out, and_2_out, and_3_out, B0, B1, B2, B3, B4, B5, B6, B7, B8,
       B9, B11, clock_out, D0_t, D1_t, D2_t, D3_t, D4_t, D6_t, D7, d_ff_2_q, DR_inc, DR_lda, I, or_1_out,
       or_2_out, or_3_out, pc_signals_1_inc, T3, T4_t, T5_t, T6_t;
  wire [2:0] alu_signals_1_out_12, selection_lines_1_out_14;
  wire [10:10] control_unit_p11;
  wire [11:0] AR, bit_extender_1_out, bit_extender_2_out, PC_q;
  wire [15:0] AC_2_q, ALU_output, bit_extender_3_out, bit_extender_4_out, DR, IR_q, multiplexer_1_out,
       ram_1_data, TR_q;

  ALU_Signals alu_signals_1 (
    .T5(T5_t), .D0(D0_t), .D1(D1_t), .D2(D2_t), .D7(D7), .I(I), .T3(T3), .B9(B9), .B7(B7), .B6(B6),
    .out_12(alu_signals_1_out_12));  // open: out_11, out_13
  PC_signals pc_signals_1 (
    .AR(AR), .D7(D7), .I(I), .T3(T3), .B2(B2), .D6(D6_t), .T6(T6_t), .DR(DR), .INC(pc_signals_1_inc));  // open: in_2
  DR_Signals u_DR (.T4(T4_t), .D1(D1_t), .D2(D2_t), .D6(D6_t), .T5(T5_t), .LDA(DR_lda), .INC(DR_inc));
  AC_Signals AC (
    .D1(D1_t), .D2(D2_t), .T5(T5_t), .B9(B9), .D7(D7), .T3(T3), .I_prime(I), .B11(B11), .B5(B5),
    .LDA(AC_lda), .CLA(AC_cla), .INC(AC_inc));
  D_Flip_Flop d_ff_1 (.clk(clock_out), .D(ALU_to_e), .Q(E), .en(1'b1));  // open: Qn, preset, reset
  Bit_Extender #(.in_width(16), .out_width(12)) bit_extender_1 (.in(multiplexer_1_out), .out(bit_extender_1_out));
  Bit_Extender #(.in_width(16), .out_width(12)) bit_extender_2 (.in(multiplexer_1_out), .out(bit_extender_2_out));
  ALU ALU (.DR(DR), .AC(AC_2_q), .to_E(ALU_to_e), .selection_lines(ALU_selection_lines), .\output (ALU_output));
  or or_1 (or_1_out, D0, D1, D2, D4);
  Clock clock (.out(clock_out));
  and and_1 (and_1_out, or_1_out, T5);
  or or_2 (or_2_out, D4, D3);
  buf and_2 (and_2_out, D6);  // AND_Gate
  Counter #(.width(12), .max('hfff)) u_AR (
    .load(load), .D(bit_extender_1_out), .count(INR), .Q(AR), .clk(clock_out), .clr(CLR));  // open: carry
  Counter #(.width(12), .max('hfff)) PC (
    .load(load_2), .D(bit_extender_2_out), .count(INR_2), .Q(PC_q), .clk(clock_out), .clr(CLR_2));  // open: carry
  Counter #(.width(16), .max('hffff)) DR_2 (
    .load(load_3), .D(multiplexer_1_out), .count(INR_3), .Q(DR), .clk(clock_out), .clr(CLR_3));  // open: carry
  Counter #(.width(16), .max('hffff)) AC_2 (
    .load(load_4), .D(ALU_output), .count(INR_4), .Q(AC_2_q), .clk(clock_out), .clr(CLR_4));  // open: carry
  Counter #(.width(16), .max('hffff)) IR (
    .load(load_5), .D(multiplexer_1_out), .count(1'b0), .Q(IR_q), .clk(clock_out), .clr(1'b0));  // open: carry
  Counter #(.width(16), .max('hffff)) TR (
    .load(load_6), .D(multiplexer_1_out), .count(INR_5), .Q(TR_q), .clk(clock_out), .clr(CLR_5));  // open: carry
  and and_3 (and_3_out, or_2_out, T4);
  RAM #(.addrWidth(12), .dataWidth(16), .bus("separate")) ram_1 (
    .addr(AR), .din(multiplexer_1_out), .data(ram_1_data), .str(Write), .clk(clock_out), .ld(Read));  // open: sel, clr
  assign bit_extender_3_out = {{4{1'b0}}, AR};  // Bit_Extender bit_extender_3
  assign bit_extender_4_out = {{4{1'b0}}, PC_q};  // Bit_Extender bit_extender_4
  or or_3 (or_3_out, and_1_out, and_3_out, and_2_out);
  D_Flip_Flop d_ff_2 (
    .clk(clock_out), .D(or_3_out), .Q(d_ff_2_q), .preset(in_28), .en(in_31), .reset(in_32));  // open: Qn
  Multiplexer #(.select(3), .width(16)) multiplexer_1 (
    .in1(bit_extender_3_out), .in2(bit_extender_4_out), .in3(DR), .in4(AC_2_q), .in5(IR_q), .in6(TR_q),
    .in7(ram_1_data), .out(multiplexer_1_out), .sel(BUS_Sel), .en(1'b1));  // open: in0
  Selection_lines selection_lines_1 (
    .D4(D4_t), .T5(T5_t), .T6(T6_t), .D3(D3_t), .T4(T4_t), .D1(D1_t), .D2(D2_t), .D6(D6_t),
    .out_14(selection_lines_1_out_14));  // open: in_4, in_5, in_6, in_8, out_13, out_15
  // Control_Unit control_unit: pin names not known; wires that end beside it: D0_t, D1_t, D2_t, D3_t, D4_t, D6_t, D7, IR_q, CLR_SC, clock_out, {B11, control_unit_p11[10], B9, B8, B7, B6, B5, B4, B3, B2, B1, B0}, I, T3, T4_t, T5_t, T6_t, T6_t
endmodule

module Control_Unit (
  input  [15:0] IR,
  input  CLR,
  output T0,
  output T1,
  output [11:0] IR_0_11,
  output T2,
  output T3,
  output T4,
  output D0,
  output T5,
  output D1,
  output T6,
  output D2,
  output T7,
  output D3,
  output T8,
  output D4,
  output T9,
  output D5,
  output T10,
  output D6,
  output T11,
  output D7,
  output T12,
  output T13,
  output T14,
  output I,
  output T15
);

  wire clock_1_out;
  wire [3:0] SC_q;

  Counter #(.width(4), .max('hf)) SC (.count(1'b1), .Q(SC_q), .clk(clock_1_out), .clr(CLR));  // open: load, D, carry
  Decoder #(.select(4)) decoder_1 (
    .out0(T0), .out1(T1), .out2(T2), .out3(T3), .out4(T4), .out5(T5), .out6(T6), .out7(T7), .out8(T8),
    .out9(T9), .out10(T10), .out11(T11), .out12(T12), .out13(T13), .out14(T14), .out15(T15), .sel(SC_q),
    .en(1'b1));
  Clock clock_1 (.out(clock_1_out));
  D_Flip_Flop d_ff_1 (.clk(clock_1_out), .D(IR[15]), .Q(I), .en(1'b1));  // open: Qn, preset, reset
  Decoder #(.select(3)) decoder_2 (
    .out0(D0), .out1(D1), .out2(D2), .out3(D3), .out4(D4), .out5(D5), .out6(D6), .out7(D7), .sel(IR[14:12]),
    .en(1'b1));

  assign IR_0_11 = IR[11:0];
endmodule

module AC_Signals (
  input  D1,
  input  D2,
  input  T5,
  input  B9,
  input  D7,
  input  T3,
  input  I_prime,
  input  B11,
  input  B5,
  output LDA,
  output CLA,
  output INC
);

  wire and_1_out, and_2_out, and_3_out, not_1_out, or_1_out;

  not not_1 (not_1_out, I_prime);
  or or_1 (or_1_out, D1, D2);
  and and_1 (and_1_out, D7, T3, not_1_out);
  and and_2 (and_2_out, or_1_out, T5);
  and and_3 (and_3_out, B9, and_1_out);
  or or_2 (LDA, and_2_out, and_3_out);
  and and_4 (CLA, and_1_out, B11);
  and and_5 (INC, and_1_out, B5);
endmodule

module DR_Signals (
  input  T4,
  input  D1,
  input  D2,
  input  D6,
  input  T5,
  output LDA,
  output INC
);

  wire or_1_out;

  or or_1 (or_1_out, D1, D2, D6);
  and and_1 (LDA, T4, or_1_out);
  and and_2 (INC, D6, T5);
endmodule

// PC
module PC_signals (
  input  [11:0] AR,
  input  [11:0] in_2,
  input  D7,
  input  I,
  input  T3,
  input  B2,
  input  D6,
  input  T6,
  input  [15:0] DR,
  output INC
);

  wire and_1_out, and_2_out, and_3_out, and_4_out, and_5_out, comparator_1_eq, comparator_2_eq, not_1_out;
  wire [15:0] bit_extender_1_out;

  not not_1 (not_1_out, I);
  assign bit_extender_1_out = {{4{1'b0}}, in_2};  // Bit_Extender bit_extender_1
  and and_1 (and_1_out, D7, not_1_out, T3);
  and and_2 (and_2_out, D6, T6);
  Comparator #(.width(16)) comparator_1 (.a(DR), .b(bit_extender_1_out), .eq(comparator_1_eq));  // open: gt, lt
  Comparator #(.width(12)) comparator_2 (.a(AR), .b(in_2), .eq(comparator_2_eq));  // open: gt, lt
  and and_3 (and_3_out, and_1_out, B2);
  and and_4 (and_4_out, and_2_out, comparator_1_eq);
  and and_5 (and_5_out, comparator_2_eq, and_3_out);
  or or_1 (INC, and_5_out, and_4_out);

  // Other names for the same wires on the sheet: _0[11:0] = in_2
endmodule

module Selection_lines (
  input  D4,
  input  T5,
  input  T6,
  input  in_4,
  input  in_5,
  input  in_6,
  input  D3,
  input  in_8,
  input  T4,
  input  D1,
  input  D2,
  input  D6,
  output out_13,
  output [2:0] out_14,
  output out_15
);

  wire and_1_out, and_2_out, and_3_out, and_4_out, and_5_out, or_1_out, or_2_out;

  and and_1 (and_1_out, D2, T5);
  and and_2 (and_2_out, T6, D6);
  or or_1 (or_1_out, D1, D2, D6);
  and and_3 (and_3_out, D4, T4);
  and and_4 (and_4_out, D3, T4);
  or or_2 (or_2_out, and_1_out, and_2_out);
  and and_5 (and_5_out, T4, or_1_out);
  Priority_Encoder priority_encoder_1 (
    .in0(in_4), .in1(and_3_out), .in2(in_5), .in3(or_2_out), .in4(and_4_out), .in5(in_6), .in6(in_8),
    .in7(and_5_out), .out(out_14), .en_in(out_15), .en_out(out_13));  // open: gs
endmodule

// ALU signals
module ALU_Signals (
  input  T5,
  input  D0,
  input  D1,
  input  D2,
  input  D7,
  input  I,
  input  T3,
  input  B9,
  input  B7,
  input  B6,
  output out_11,
  output [2:0] out_12,
  output out_13
);

  wire and_1_out, and_2_out, and_3_out, and_4_out, and_5_out, and_6_out, and_7_out, not_1_out;

  not not_1 (not_1_out, I);
  and and_1 (and_1_out, T5, D1);
  and and_2 (and_2_out, D7, not_1_out, T3);
  and and_3 (and_3_out, T5, D2);
  and and_4 (and_4_out, T5, D0);
  and and_5 (and_5_out, and_2_out, B9);
  and and_6 (and_6_out, and_2_out, B7);
  and and_7 (and_7_out, and_2_out, B6);
  Priority_Encoder priority_encoder_1 (
    .in0(and_4_out), .in1(and_1_out), .in2(and_3_out), .in3(and_5_out), .in4(and_6_out), .in5(and_7_out),
    .out(out_12), .en_in(out_13), .en_out(out_11));  // open: in6, in7, gs
endmodule
